// Logisim project problem1.circ as structural Verilog: 13 circuits, main circuit main
module main (
  output [3:0] out_1
);

  wire ALU_zero, armux, clock, fetch, irld, memld, mux, pcinc, pcld, regld, zf, zfld;
  wire [2:0] dst, src1, src2;
  wire [5:0] opcode;
  wire [11:0] adder_1_out, alu2_12, IR_addr, multiplexer_1_out, pc_1_output, R7_12, ram_1_data;
  wire [15:0] ALU_aluresult, multiplexer_2_out, multiplexer_3_out, registerbank_1_dout1,
       registerbank_1_dout2, registerbank_1_dout3, registerbank_1_dout4, registerbank_1_dout5,
       registerbank_1_dout6, registerbank_1_dout7;
  wire [15:12] alu2_16, R7_16;

  Clock clock_1 (.out(clock));
  Adder #(.width(12)) adder_1 (.a(pc_1_output), .b(IR_addr), .out(adder_1_out));  // open: cin, cout
  Multiplexer #(.width(12), .enable("false")) multiplexer_1 (
    .in0(pc_1_output), .in1(alu2_12), .out(multiplexer_1_out), .sel(armux));
  PC pc_1 (.pc_load(pcld), .clock(clock), .\output (pc_1_output), .increment(pcinc), .input_data(adder_1_out));
  RAM #(.addrWidth(12), .dataWidth(16), .bus("separate")) ram_1 (
    .addr(multiplexer_1_out), .din(multiplexer_3_out), .data({out_1, ram_1_data}), .str(memld), .clk(clock));  // open: sel, ld, clr
  Registerbank registerbank_1 (
    .Reg_Select(dst), .Reg_load(regld), .Data_In(multiplexer_2_out), .DOUT1(registerbank_1_dout1),
    .DOUT2(registerbank_1_dout2), .DOUT3(registerbank_1_dout3), .DOUT4(registerbank_1_dout4),
    .DOUT5(registerbank_1_dout5), .DOUT6(registerbank_1_dout6), .DOUT7(registerbank_1_dout7),
    .DOUT8({R7_16, R7_12}), .clock(clock));
  _1_bit_Register u_ZF (.Data(ALU_zero), .Output(zf), .Load(zfld), .clk(clock));
  Multiplexer #(.width(16), .enable("false")) multiplexer_2 (
    .in0(ALU_aluresult), .in1({out_1, ram_1_data}), .out(multiplexer_2_out), .sel(mux));
  Multiplexer #(.select(3), .width(16), .enable("false")) multiplexer_3 (
    .in0(registerbank_1_dout1), .in1(registerbank_1_dout2), .in2(registerbank_1_dout3),
    .in3(registerbank_1_dout4), .in4(registerbank_1_dout5), .in5(registerbank_1_dout6),
    .in6(registerbank_1_dout7), .in7({R7_16, R7_12}), .out(multiplexer_3_out), .sel(src1));
  ALU ALU (.A(multiplexer_3_out), .B({alu2_16, alu2_12}), .AluOp(opcode), .AluResult(ALU_aluresult), .Zero(ALU_zero));
  Multiplexer #(.select(3), .width(16), .enable("false")) multiplexer_4 (
    .in0(registerbank_1_dout1), .in1(registerbank_1_dout2), .in2(registerbank_1_dout3),
    .in3(registerbank_1_dout4), .in4(registerbank_1_dout5), .in5(registerbank_1_dout6),
    .in6(registerbank_1_dout7), .in7({R7_16, R7_12}), .out({alu2_16, alu2_12}), .sel(src2));
  Control_Unit Control_Unit (
    .opcode(out_1), .ZF(zf), .clock(clock), .out_4({fetch, pcld, pcinc, armux, mux, regld, zfld, memld, irld}));
  Instruction_Register IR (
    .in_1(ram_1_data), .src1(src1), .aluop(opcode), .src2(src2), .dst(dst), .addr(IR_addr), .clock(clock),
    .load(irld));

  // Other names for the same wires on the sheet: alu2_16[11:0] = alu2_12; R7_16[11:0] = R7_12

  // Notes on the sheet:
  //   Memory
  //   Control Signals
endmodule

module Control_Unit (
  input  [3:0] opcode,
  input  ZF,
  input  clock,
  output [8:0] out_4
);

  wire not_1_out, not_2_out, not_3_out;
  wire [1:1] and_1_out;
  wire [3:0] multiplexer_1_out, multiplexer_2_out, n4_bits_register_1_out_3;

  not not_1 (not_1_out, opcode[0]);
  and and_1 (and_1_out[1], not_1_out, not_2_out, opcode[2], not_3_out);
  not not_2 (not_2_out, opcode[1]);
  not not_3 (not_3_out, opcode[3]);
  Multiplexer #(.select(2), .width(4), .enable("false")) multiplexer_1 (
    .in0(opcode), .in1(opcode), .in2(4'b0000), .in3(4'b0101), .out(multiplexer_1_out),
    .sel({and_1_out[1], ZF}));
  Multiplexer #(.width(4), .enable("false")) multiplexer_2 (
    .in0(4'b0000), .in1(multiplexer_1_out), .out(multiplexer_2_out), .sel(out_4[8]));
  _4_bits_Register u_4_bits_register_1 (.in_1(multiplexer_2_out), .in_2(clock), .out_3(n4_bits_register_1_out_3));
  ROM #(.addrWidth(4), .dataWidth(9)) rom_1 (.addr(n4_bits_register_1_out_3), .data(out_4));  // open: sel

  // Notes on the sheet:
  //   contents of rom_1 (hex, n*v repeats v):
  //   141 54 34 22 0 80 0 18
endmodule

module ALU (
  input  [15:0] A,
  input  [15:0] B,
  input  [5:0] AluOp,
  output [15:0] AluResult,
  output Zero
);

  wire [15:0] adder_1_out, adder_2_out, Bitwise_And_out, Bitwise_Not_out, Bitwise_Or_out, Bitwise_Xor_out,
       multiplexer_1_out, subtractor_1_out, subtractor_2_out;

  assign Bitwise_And_out = A & B;  // AND_Gate Bitwise_And, 16 bits wide
  assign Bitwise_Or_out = A | B;  // OR_Gate Bitwise_Or, 16 bits wide
  assign Bitwise_Xor_out = A ^ B;  // XOR_Gate Bitwise_Xor, 16 bits wide
  assign Bitwise_Not_out = ~B;  // NOT_Gate Bitwise_Not, 16 bits wide
  Adder #(.width(16)) adder_1 (.a(A), .b(B), .out(adder_1_out));  // open: cin, cout
  Subtractor #(.width(16)) subtractor_1 (.a(A), .b(B), .out(subtractor_1_out));  // open: bin, bout
  Adder #(.width(16)) adder_2 (.a(B), .b(16'h1), .out(adder_2_out));  // open: cin, cout
  Subtractor #(.width(16)) subtractor_2 (.a(B), .b(16'h1), .out(subtractor_2_out));  // open: bin, bout
  Multiplexer #(.select(3), .width(16)) multiplexer_1 (
    .in0(Bitwise_Not_out), .in1(B), .in2(adder_2_out), .in3(subtractor_2_out), .out(multiplexer_1_out),
    .sel({1'b0, AluOp[1:0]}));  // open: in4, in5, in6, in7, en
  Multiplexer #(.select(3), .width(16)) multiplexer_2 (
    .in0(adder_1_out), .in1(subtractor_1_out), .in2(Bitwise_And_out), .in3(Bitwise_Or_out),
    .in4(Bitwise_Xor_out), .in7(multiplexer_1_out), .out(AluResult), .sel(AluOp[5:3]));  // open: in5, in6, en
  nor nor_1 (Zero, AluResult[0], AluResult[1], AluResult[2], AluResult[3], AluResult[4], AluResult[5], AluResult[6], AluResult[7], AluResult[9], AluResult[10], AluResult[11], AluResult[12], AluResult[13], AluResult[14], AluResult[15], AluResult[8]);

  // Notes on the sheet:
  //   Adder
  //   Substractor
  //   Move
endmodule

module RegBank (
  input  in_1,
  input  in_2,
  output out_3
);

  wire clock_1_out;

  Clock clock_1 (.out(clock_1_out));
  S_R_Flip_Flop s_r_ff_1 (.S(in_1), .R(in_2), .Q(out_3), .preset(clock_1_out));  // open: clk, Qn, reset, en
endmodule

module _1_bit_Register (
  input  Data,
  input  Load,
  input  clk,
  output Output
);

  wire and_1_out, and_2_out, not_1_out;

  and and_1 (and_1_out, Data, Load);
  not not_1 (not_1_out, Data);
  and and_2 (and_2_out, not_1_out, Load);
  S_R_Flip_Flop s_r_ff_1 (.S(and_1_out), .clk(clk), .R(and_2_out), .Q(Output));  // open: Qn, preset, reset, en
endmodule

module _16_bits_Register (
  input  [15:0] Data,
  input  load,
  input  clk,
  output [15:0] out_4
);

  _1_bit_Register u_1_bit_register_1 (.Data(Data[0]), .Output(out_4[0]), .Load(load), .clk(clk));
  _1_bit_Register u_1_bit_register_2 (.Data(Data[1]), .Output(out_4[1]), .Load(load), .clk(clk));
  _1_bit_Register u_1_bit_register_3 (.Data(Data[2]), .Output(out_4[2]), .Load(load), .clk(clk));
  _1_bit_Register u_1_bit_register_4 (.Data(Data[3]), .Output(out_4[3]), .Load(load), .clk(clk));
  _1_bit_Register u_1_bit_register_5 (.Data(Data[4]), .Output(out_4[4]), .Load(load), .clk(clk));
  _1_bit_Register u_1_bit_register_6 (.Data(Data[5]), .Output(out_4[5]), .Load(load), .clk(clk));
  _1_bit_Register u_1_bit_register_7 (.Data(Data[6]), .Output(out_4[6]), .Load(load), .clk(clk));
  _1_bit_Register u_1_bit_register_8 (.Data(Data[7]), .Output(out_4[7]), .Load(load), .clk(clk));
  _1_bit_Register u_1_bit_register_9 (.Data(Data[8]), .Output(out_4[8]), .Load(load), .clk(clk));
  _1_bit_Register u_1_bit_register_10 (.Data(Data[9]), .Output(out_4[9]), .Load(load), .clk(clk));
  _1_bit_Register u_1_bit_register_11 (.Data(Data[10]), .Output(out_4[10]), .Load(load), .clk(clk));
  _1_bit_Register u_1_bit_register_12 (.Data(Data[11]), .Output(out_4[11]), .Load(load), .clk(clk));
  _1_bit_Register u_1_bit_register_13 (.Data(Data[12]), .Output(out_4[12]), .Load(load), .clk(clk));
  _1_bit_Register u_1_bit_register_14 (.Data(Data[13]), .Output(out_4[13]), .Load(load), .clk(clk));
  _1_bit_Register u_1_bit_register_15 (.Data(Data[14]), .Output(out_4[14]), .Load(load), .clk(clk));
  _1_bit_Register u_1_bit_register_16 (.Data(Data[15]), .Output(out_4[15]), .Load(load), .clk(clk));
endmodule

// Reg bank
module Registerbank (
  input  [2:0] Reg_Select,
  input  Reg_load,
  input  [15:0] Data_In,
  input  clock,
  output [15:0] DOUT1,
  output [15:0] DOUT2,
  output [15:0] DOUT3,
  output [15:0] DOUT4,
  output [15:0] DOUT5,
  output [15:0] DOUT6,
  output [15:0] DOUT7,
  output [15:0] DOUT8
);

  wire and_1_out, and_2_out, and_3_out, and_4_out, and_5_out, and_6_out, and_7_out, and_8_out,
       decoder_1_out0, decoder_1_out1, decoder_1_out2, decoder_1_out3, decoder_1_out4, decoder_1_out5,
       decoder_1_out6, decoder_1_out7;

  Decoder #(.select(3)) decoder_1 (
    .out0(decoder_1_out0), .out1(decoder_1_out1), .out2(decoder_1_out2), .out3(decoder_1_out3),
    .out4(decoder_1_out4), .out5(decoder_1_out5), .out6(decoder_1_out6), .out7(decoder_1_out7),
    .sel(Reg_Select));  // open: en
  and and_1 (and_1_out, decoder_1_out0, Reg_load);
  and and_2 (and_2_out, decoder_1_out1, Reg_load);
  and and_3 (and_3_out, decoder_1_out2, Reg_load);
  and and_4 (and_4_out, decoder_1_out3, Reg_load);
  and and_5 (and_5_out, decoder_1_out4, Reg_load);
  and and_6 (and_6_out, decoder_1_out5, Reg_load);
  and and_7 (and_7_out, decoder_1_out6, Reg_load);
  and and_8 (and_8_out, decoder_1_out7, Reg_load);
  _16_bits_Register Register_0 (.Data(Data_In), .out_4(DOUT1), .load(and_1_out), .clk(clock));
  _16_bits_Register Register_1 (.Data(Data_In), .out_4(DOUT2), .load(and_2_out), .clk(clock));
  _16_bits_Register Register_2 (.Data(Data_In), .out_4(DOUT3), .load(and_3_out), .clk(clock));
  _16_bits_Register Register_3 (.Data(Data_In), .out_4(DOUT4), .load(and_4_out), .clk(clock));
  _16_bits_Register Register_4 (.Data(Data_In), .out_4(DOUT5), .load(and_5_out), .clk(clock));
  _16_bits_Register Register_5 (.Data(Data_In), .out_4(DOUT6), .load(and_6_out), .clk(clock));
  _16_bits_Register Register_6 (.Data(Data_In), .out_4(DOUT7), .load(and_7_out), .clk(clock));
  _16_bits_Register Register_7 (.Data(Data_In), .out_4(DOUT8), .load(and_8_out), .clk(clock));
endmodule

module Instruction_Register (
  input  [11:0] in_1,
  input  load,
  input  clock,
  output [11:0] addr,
  output [2:0] dst,
  output [2:0] src1,
  output [2:0] src2,
  output [5:0] aluop
);

  _12_bits_Register u_12_bits_register_1 (.Data(in_1), .load(load), .clk(clock), .out_4(addr));

  assign aluop = addr[11:6];
  assign dst = addr[2:0];
  assign src1 = addr[8:6];
  assign src2 = addr[5:3];
endmodule

module PC (
  input  [11:0] input_data,
  input  pc_load,
  input  clock,
  input  increment,
  output [11:0] \output 
);

  wire or_1_out;
  wire [11:0] adder_1_out, multiplexer_1_out;

  or or_1 (or_1_out, pc_load, increment);
  _12_bits_Register u_12_bits_register_1 (.Data(multiplexer_1_out), .load(or_1_out), .clk(clock), .out_4(\output ));
  Adder #(.width(12)) adder_1 (.a(\output ), .b(12'h1), .out(adder_1_out));  // open: cin, cout
  Multiplexer #(.width(12), .enable("false")) multiplexer_1 (
    .in0(input_data), .in1(adder_1_out), .out(multiplexer_1_out), .sel(increment));
endmodule

module _12_bits_Register (
  input  [11:0] Data,
  input  load,
  input  clk,
  output [11:0] out_4
);

  _1_bit_Register u_1_bit_register_1 (.Data(Data[0]), .Output(out_4[0]), .Load(load), .clk(clk));
  _1_bit_Register u_1_bit_register_2 (.Data(Data[1]), .Output(out_4[1]), .Load(load), .clk(clk));
  _1_bit_Register u_1_bit_register_3 (.Data(Data[2]), .Output(out_4[2]), .Load(load), .clk(clk));
  _1_bit_Register u_1_bit_register_4 (.Data(Data[3]), .Output(out_4[3]), .Load(load), .clk(clk));
  _1_bit_Register u_1_bit_register_5 (.Data(Data[4]), .Output(out_4[4]), .Load(load), .clk(clk));
  _1_bit_Register u_1_bit_register_6 (.Data(Data[5]), .Output(out_4[5]), .Load(load), .clk(clk));
  _1_bit_Register u_1_bit_register_7 (.Data(Data[6]), .Output(out_4[6]), .Load(load), .clk(clk));
  _1_bit_Register u_1_bit_register_8 (.Data(Data[7]), .Output(out_4[7]), .Load(load), .clk(clk));
  _1_bit_Register u_1_bit_register_9 (.Data(Data[8]), .Output(out_4[8]), .Load(load), .clk(clk));
  _1_bit_Register u_1_bit_register_10 (.Data(Data[9]), .Output(out_4[9]), .Load(load), .clk(clk));
  _1_bit_Register u_1_bit_register_11 (.Data(Data[10]), .Output(out_4[10]), .Load(load), .clk(clk));
  _1_bit_Register u_1_bit_register_12 (.Data(Data[11]), .Output(out_4[11]), .Load(load), .clk(clk));
endmodule

module _4_bits_Register (
  input  [3:0] in_1,
  input  in_2,
  output [3:0] out_3
);

  _1_bit_Register u_1_bit_register_1 (.Data(in_1[0]), .Output(out_3[0]), .Load(1'b1), .clk(in_2));
  _1_bit_Register u_1_bit_register_2 (.Data(in_1[1]), .Output(out_3[1]), .Load(1'b1), .clk(in_2));
  _1_bit_Register u_1_bit_register_3 (.Data(in_1[2]), .Output(out_3[2]), .Load(1'b1), .clk(in_2));
  _1_bit_Register u_1_bit_register_4 (.Data(in_1[3]), .Output(out_3[3]), .Load(1'b1), .clk(in_2));
endmodule

module PC_deneme (
  input  [11:0] input_data,
  input  pc_load,
  input  clock,
  input  increment,
  output [11:0] \output 
);

  wire or_1_out;
  wire [11:0] adder_1_out, adder_2_out, multiplexer_1_out;

  Adder #(.width(12)) adder_1 (.a(\output ), .b(12'h1), .out(adder_1_out));  // open: cin, cout
  Adder #(.width(12)) adder_2 (.a(input_data), .b(\output ), .out(adder_2_out));  // open: cin, cout
  Multiplexer #(.width(12), .enable("false")) multiplexer_1 (
    .in0(adder_1_out), .in1(adder_2_out), .out(multiplexer_1_out), .sel(pc_load));
  or or_1 (or_1_out, pc_load, increment);
  _12_bits_Register u_12_bits_register_1 (.Data(multiplexer_1_out), .load(or_1_out), .clk(clock), .out_4(\output ));
endmodule

module signextend12_16 (
  input  [11:0] in_1,
  output [15:0] out_2
);


  assign out_2 = {{5{in_1[11]}}, in_1[10:0]};
endmodule
